# Fritzing sketch Incubator-Fritzing (saved by Fritzing 0.9.2b)
breadboards: 4

parts:
  80mm_Fan = DC Motor
  MOSFET1 = Basic FET N-Channel [package="TO220 [THT]"]
  LED1 = LED - 5mm [color="White (4500K)" package="5 mm [THT]"]
  Pushbutton_1 = Pushbutton [package="[THT]"]
  Pushbutton_2 = Pushbutton [package="[THT]"]
  R6_-_Pull_down_for_MOSFET_1 = Resistor [tolerance=±5% resistance=10k package=THT]
  R7_-_For_LED1 = Resistor [tolerance=±5% resistance=220 package=THT]
  Diode1 = Rectifier Diode [part_number=1N4001 package="300 mil [THT]"]
  Power_plug1 = Power plug
  R8_-_Pull_up_for_Temp1 = Resistor [tolerance=±5% resistance=10k package=THT]
  R9_-_Pull_down_for_button_1 = Resistor [tolerance=±5% resistance=10k package=THT]
  R10_-_Pull_down_for_button_2 = Resistor [tolerance=±5% resistance=10k package=THT]
  R1 = Temperature Sensor (Thermistor) [thermistor_type=NTC package=THT]
  Switch_for_LED1 = Pushbutton [package=THT]
  Arduino1 = Arduino Uno (Rev3)
  LCD2 = LCD screen  # not connected
  U2 = mystery part, 4 pins [chip_label=I2C spacing=300mil]
  MOSFET2 = Basic FET N-Channel [package="TO220 [THT]"]
  R6_-_Pull_down_for_MOSFET_2 = Resistor [tolerance=±5% resistance=10k package=THT]
  R2 = Resistor [tolerance=±5% resistance=1.5 power=22W package=THT]

nets (from the schematic view):
  VCC: 80mm_Fan.pin_1, Diode1.cathode, Power_plug1.VCC, Arduino1.VIN, R2.Pin_0
  N1: 80mm_Fan.pin_2, MOSFET1.drain, Diode1.anode
  N2: MOSFET1.gate, R6_-_Pull_down_for_MOSFET_1.Pin_1, Arduino1.D5_PWM
  GND: MOSFET1.source, LED1.cathode, R6_-_Pull_down_for_MOSFET_1.Pin_0, Power_plug1.GND, R9_-_Pull_down_for_button_1.Pin_0, R10_-_Pull_down_for_button_2.Pin_1, R1.pin_0, Arduino1.GND, U2.pin4, MOSFET2.source, R6_-_Pull_down_for_MOSFET_2.Pin_0
  N3: LED1.anode, R7_-_For_LED1.Pin_1
  N4: Pushbutton_1.Pin_1, Pushbutton_1.Pin_2, R9_-_Pull_down_for_button_1.Pin_1, Arduino1.D11_PWM/MOSI
  N5: Pushbutton_1.Pin_3, Pushbutton_1.Pin_4, Pushbutton_2.Pin_3, Pushbutton_2.Pin_4, Switch_for_LED1.leg1, Arduino1.5V, U2.pin3
  N6: Pushbutton_2.Pin_1, Pushbutton_2.Pin_2, R10_-_Pull_down_for_button_2.Pin_0, Arduino1.D12/MISO
  N7: R7_-_For_LED1.Pin_0, Switch_for_LED1.leg0
  N8: R8_-_Pull_up_for_Temp1.Pin_1, R1.pin_1, Arduino1.A0
  N9: Arduino1.A4/SDA, U2.pin2
  N10: Arduino1.A5/SCL, U2.pin1
  N11: Arduino1.D6_PWM, MOSFET2.gate, R6_-_Pull_down_for_MOSFET_2.Pin_1
  N12: MOSFET2.drain, R2.Pin_1

notes:
  12 V power supply
  Fan
  Fan controller
  Temp Sensor
  Light & Switch
  User interface buttons
  Light Switch
  Push buttons
  Fan conroller
  12V power supply
  LCD I2C interface
  SCL - A5
  SDA - A4
  Vcc
  Gnd
  Heating Pad
  LCD I2C controller
